// Logisim project 19101284.circ as structural Verilog: 16 circuits, main circuit main
module main (
);

  wire button_1_out, button_2_out, ChSelector_out, clock_1_out, MonitorSelector_out;
  wire [1:0] twobitcounter_1_d, twobitcounter_2_d;
  wire [9:0] volumecontroller_1_out_4, volumecontroller_1_out_5, volumecontroller_1_out_6,
       volumecontroller_1_out_7;
  wire [15:0] demultiplexer_1_out0, demultiplexer_1_out0_2, demultiplexer_1_out0_3, demultiplexer_1_out0_4,
       demultiplexer_2_out0, demultiplexer_2_out0_2, demultiplexer_2_out0_3, demultiplexer_2_out0_4,
       demultiplexer_2_out1, demultiplexer_2_out1_2, demultiplexer_2_out1_3, demultiplexer_2_out1_4,
       demultiplexer_3_out0, demultiplexer_3_out0_2, demultiplexer_3_out0_3, demultiplexer_3_out0_4,
       demultiplexer_3_out1, demultiplexer_3_out1_2, demultiplexer_3_out1_3, demultiplexer_3_out1_4,
       demultiplexer_4_out0, demultiplexer_4_out0_2, demultiplexer_4_out0_3, demultiplexer_4_out0_4,
       demultiplexer_4_out1, demultiplexer_4_out1_2, demultiplexer_4_out1_3, demultiplexer_4_out1_4;
  wire [63:0] channelcontroller_1_l1, channelcontroller_1_l2, channelcontroller_1_l3, channelcontroller_1_l4,
       demultiplexer_1_out1, demultiplexer_1_out2, demultiplexer_1_out3, demultiplexer_2_out2,
       demultiplexer_2_out3, demultiplexer_3_out2, demultiplexer_3_out3, demultiplexer_4_out2,
       demultiplexer_4_out3;

  Clock clock_1 (.out(clock_1_out));
  ChannelController channelcontroller_1 (
    .CLK(clock_1_out), .in_2(twobitcounter_2_d), .L1(channelcontroller_1_l1), .L2(channelcontroller_1_l2),
    .L3(channelcontroller_1_l3), .L4(channelcontroller_1_l4));
  Demultiplexer #(.select(2), .width(64)) demultiplexer_1 (
    .out0({demultiplexer_1_out0_4, demultiplexer_1_out0_3, demultiplexer_1_out0_2, demultiplexer_1_out0}),
    .out1(demultiplexer_1_out1), .out2(demultiplexer_1_out2), .out3(demultiplexer_1_out3),
    .in(channelcontroller_1_l1), .sel(twobitcounter_1_d));
  Demultiplexer #(.select(2), .width(64)) demultiplexer_2 (
    .out0({demultiplexer_2_out0_4, demultiplexer_2_out0_3, demultiplexer_2_out0_2, demultiplexer_2_out0}),
    .out1({demultiplexer_2_out1_4, demultiplexer_2_out1_3, demultiplexer_2_out1_2, demultiplexer_2_out1}),
    .out2(demultiplexer_2_out2), .out3(demultiplexer_2_out3), .in(channelcontroller_1_l2),
    .sel(twobitcounter_1_d));
  Demultiplexer #(.select(2), .width(64)) demultiplexer_3 (
    .out0({demultiplexer_3_out0_4, demultiplexer_3_out0_3, demultiplexer_3_out0_2, demultiplexer_3_out0}),
    .out1({demultiplexer_3_out1_4, demultiplexer_3_out1_3, demultiplexer_3_out1_2, demultiplexer_3_out1}),
    .out2(demultiplexer_3_out2), .out3(demultiplexer_3_out3), .in(channelcontroller_1_l3),
    .sel(twobitcounter_1_d));
  Demultiplexer #(.select(2), .width(64)) demultiplexer_4 (
    .out0({demultiplexer_4_out0_4, demultiplexer_4_out0_3, demultiplexer_4_out0_2, demultiplexer_4_out0}),
    .out1({demultiplexer_4_out1_4, demultiplexer_4_out1_3, demultiplexer_4_out1_2, demultiplexer_4_out1}),
    .out2(demultiplexer_4_out2), .out3(demultiplexer_4_out3), .in(channelcontroller_1_l4),
    .sel(twobitcounter_1_d));
  DotMatrix #(.matrixcols(16), .matrixrows(16)) dotmatrix_1 (
    .col0(demultiplexer_1_out3[63:48]), .col1(demultiplexer_1_out3[47:32]),
    .col2(demultiplexer_1_out3[31:16]), .col3(demultiplexer_1_out3[15:0]),
    .col4(demultiplexer_2_out3[63:48]), .col5(demultiplexer_2_out3[47:32]),
    .col6(demultiplexer_2_out3[31:16]), .col7(demultiplexer_2_out3[15:0]),
    .col8(demultiplexer_3_out3[63:48]), .col9(demultiplexer_3_out3[47:32]),
    .col10(demultiplexer_3_out3[31:16]), .col11(demultiplexer_3_out3[15:0]),
    .col12(demultiplexer_4_out3[63:48]), .col13(demultiplexer_4_out3[47:32]),
    .col14(demultiplexer_4_out3[31:16]), .col15(demultiplexer_4_out3[15:0]));
  TwoBitCounter twobitcounter_1 (.CLK(MonitorSelector_out), .D(twobitcounter_1_d));
  TwoBitCounter twobitcounter_2 (.CLK(ChSelector_out), .D(twobitcounter_2_d));
  DotMatrix #(.matrixcols(2), .matrixrows(10)) dotmatrix_2 (
    .col0(volumecontroller_1_out_7), .col1(volumecontroller_1_out_7));
  Button MonitorSelector (.out(MonitorSelector_out));
  Button ChSelector (.out(ChSelector_out));
  Hex_Digit_Display #(.decimalPoint("false")) Monitor (.value({2'b00, twobitcounter_1_d}));
  DotMatrix #(.matrixcols(16), .matrixrows(16)) dotmatrix_3 (
    .col0(demultiplexer_1_out2[63:48]), .col1(demultiplexer_1_out2[47:32]),
    .col2(demultiplexer_1_out2[31:16]), .col3(demultiplexer_1_out2[15:0]),
    .col4(demultiplexer_2_out2[63:48]), .col5(demultiplexer_2_out2[47:32]),
    .col6(demultiplexer_2_out2[31:16]), .col7(demultiplexer_2_out2[15:0]),
    .col8(demultiplexer_3_out2[63:48]), .col9(demultiplexer_3_out2[47:32]),
    .col10(demultiplexer_3_out2[31:16]), .col11(demultiplexer_3_out2[15:0]),
    .col12(demultiplexer_4_out2[63:48]), .col13(demultiplexer_4_out2[47:32]),
    .col14(demultiplexer_4_out2[31:16]), .col15(demultiplexer_4_out2[15:0]));
  Hex_Digit_Display #(.decimalPoint("false")) Ch (.value({2'b00, twobitcounter_2_d}));
  Button button_1 (.out(button_1_out));
  Button button_2 (.out(button_2_out));
  DotMatrix #(.matrixcols(2), .matrixrows(10)) dotmatrix_4 (
    .col0(volumecontroller_1_out_6), .col1(volumecontroller_1_out_6));
  VolumeController volumecontroller_1 (
    .Up(button_1_out), .Down(button_2_out), .ch(twobitcounter_1_d), .out_4(volumecontroller_1_out_4),
    .out_5(volumecontroller_1_out_5), .out_6(volumecontroller_1_out_6), .out_7(volumecontroller_1_out_7));
  DotMatrix #(.matrixcols(16), .matrixrows(16)) dotmatrix_5 (
    .col0(demultiplexer_1_out1[63:48]), .col1(demultiplexer_1_out1[47:32]),
    .col2(demultiplexer_1_out1[31:16]), .col3(demultiplexer_1_out1[15:0]), .col4(demultiplexer_2_out1_4),
    .col5(demultiplexer_2_out1_3), .col6(demultiplexer_2_out1_2), .col7(demultiplexer_2_out1),
    .col8(demultiplexer_3_out1_4), .col9(demultiplexer_3_out1_3), .col10(demultiplexer_3_out1_2),
    .col11(demultiplexer_3_out1), .col12(demultiplexer_4_out1_4), .col13(demultiplexer_4_out1_3),
    .col14(demultiplexer_4_out1_2), .col15(demultiplexer_4_out1));
  DotMatrix #(.matrixcols(2), .matrixrows(10)) dotmatrix_6 (
    .col0(volumecontroller_1_out_5), .col1(volumecontroller_1_out_5));
  DotMatrix #(.matrixcols(16), .matrixrows(16)) dotmatrix_7 (
    .col0(demultiplexer_1_out0_4), .col1(demultiplexer_1_out0_3), .col2(demultiplexer_1_out0_2),
    .col3(demultiplexer_1_out0), .col4(demultiplexer_2_out0_4), .col5(demultiplexer_2_out0_3),
    .col6(demultiplexer_2_out0_2), .col7(demultiplexer_2_out0), .col8(demultiplexer_3_out0_4),
    .col9(demultiplexer_3_out0_3), .col10(demultiplexer_3_out0_2), .col11(demultiplexer_3_out0),
    .col12(demultiplexer_4_out0_4), .col13(demultiplexer_4_out0_3), .col14(demultiplexer_4_out0_2),
    .col15(demultiplexer_4_out0));
  DotMatrix #(.matrixcols(2), .matrixrows(10)) dotmatrix_8 (
    .col0(volumecontroller_1_out_4), .col1(volumecontroller_1_out_4));
endmodule

module HalfAdder (
  input  A,
  input  B,
  output S,
  output C
);

  xor xor_1 (S, A, B);
  and and_1 (C, A, B);
endmodule

module FullAdder (
  input  A,
  input  B,
  input  C_in,
  output S,
  output C_out
);

  wire halfadder_1_c, halfadder_1_s, halfadder_2_c;

  HalfAdder halfadder_1 (.A(A), .B(B), .S(halfadder_1_s), .C(halfadder_1_c));
  HalfAdder halfadder_2 (.A(halfadder_1_s), .B(C_in), .S(S), .C(halfadder_2_c));
  or or_1 (C_out, halfadder_1_c, halfadder_2_c);
endmodule

module MyCounter (
  input  CLK,
  output [7:0] D
);

  wire and_1_out, and_2_out, and_3_out, and_4_out, and_5_out, and_6_out;

  J_K_Flip_Flop j_k_ff_1 (.J(1'b1), .K(1'b1), .clk(CLK), .Q(D[0]));  // open: Qn, preset, reset
  J_K_Flip_Flop j_k_ff_2 (.J(D[0]), .K(D[0]), .clk(CLK), .Q(D[1]));  // open: Qn, preset, reset
  and and_1 (and_1_out, D[0], D[1]);
  J_K_Flip_Flop j_k_ff_3 (.J(and_1_out), .K(and_1_out), .clk(CLK), .Q(D[2]));  // open: Qn, preset, reset
  and and_2 (and_2_out, and_1_out, D[2]);
  J_K_Flip_Flop j_k_ff_4 (.J(and_2_out), .K(and_2_out), .clk(CLK), .Q(D[3]));  // open: Qn, preset, reset
  and and_3 (and_3_out, and_2_out, D[3]);
  J_K_Flip_Flop j_k_ff_5 (.J(and_3_out), .K(and_3_out), .clk(CLK), .Q(D[4]));  // open: Qn, preset, reset
  and and_4 (and_4_out, and_3_out, D[4]);
  J_K_Flip_Flop j_k_ff_6 (.J(and_4_out), .K(and_4_out), .clk(CLK), .Q(D[5]));  // open: Qn, preset, reset
  and and_5 (and_5_out, and_4_out, D[5]);
  J_K_Flip_Flop j_k_ff_7 (.J(and_5_out), .K(and_5_out), .clk(CLK), .Q(D[6]));  // open: Qn, preset, reset
  and and_6 (and_6_out, and_5_out, D[6]);
  J_K_Flip_Flop j_k_ff_8 (.J(and_6_out), .K(and_6_out), .clk(CLK), .Q(D[7]));  // open: Qn, preset, reset
endmodule

module EightBitAdder (
  input  [7:0] A,
  input  [7:0] B,
  output [7:0] S,
  output OVR
);

  wire fulladder_1_c_out, fulladder_2_c_out, fulladder_3_c_out, fulladder_4_c_out, fulladder_5_c_out,
       fulladder_6_c_out, fulladder_7_c_out;

  FullAdder fulladder_1 (.A(A[0]), .B(B[0]), .C_in(1'b0), .S(S[0]), .C_out(fulladder_1_c_out));
  FullAdder fulladder_2 (.A(A[1]), .B(B[1]), .C_in(fulladder_1_c_out), .S(S[1]), .C_out(fulladder_2_c_out));
  FullAdder fulladder_3 (.A(A[2]), .B(B[2]), .C_in(fulladder_2_c_out), .S(S[2]), .C_out(fulladder_3_c_out));
  FullAdder fulladder_4 (.A(A[3]), .B(B[3]), .C_in(fulladder_3_c_out), .S(S[3]), .C_out(fulladder_4_c_out));
  FullAdder fulladder_5 (.A(A[4]), .B(B[4]), .C_in(fulladder_4_c_out), .S(S[4]), .C_out(fulladder_5_c_out));
  FullAdder fulladder_6 (.A(A[5]), .B(B[5]), .C_in(fulladder_5_c_out), .S(S[5]), .C_out(fulladder_6_c_out));
  FullAdder fulladder_7 (.A(A[6]), .B(B[6]), .C_in(fulladder_6_c_out), .S(S[6]), .C_out(fulladder_7_c_out));
  FullAdder fulladder_8 (.A(A[7]), .B(B[7]), .C_in(fulladder_7_c_out), .S(S[7]), .C_out(OVR));
endmodule

module OneOfTwoDecoder (
  input  A,
  input  B,
  output Y0,
  output Y1,
  output Y2,
  output Y3
);

  wire not_1_out, not_2_out;

  not not_1 (not_1_out, A);
  not not_2 (not_2_out, B);
  and and_1 (Y0, not_1_out, not_2_out);
  and and_2 (Y1, A, not_2_out);
  and and_3 (Y2, not_1_out, B);
  and and_4 (Y3, A, B);

  // Notes on the sheet:
  //   OneOfTwoDecoder: Not
endmodule

module TwoBitCounter (
  input  CLK,
  output [1:0] D
);

  J_K_Flip_Flop j_k_ff_1 (.J(1'b1), .K(1'b1), .clk(CLK), .Q(D[0]));  // open: Qn, preset, reset
  J_K_Flip_Flop j_k_ff_2 (.J(D[0]), .K(D[0]), .clk(CLK), .Q(D[1]));  // open: Qn, preset, reset
endmodule

module LedMatrixSimulator (
  input  [7:0] in_1,
  input  [7:0] in_2,
  input  [7:0] in_3,
  input  [7:0] in_4,
  input  [7:0] in_5,
  input  [7:0] in_6,
  input  [7:0] in_7,
  input  [7:0] in_8,
  input  [7:0] in_9,
  input  [7:0] in_10,
  input  [7:0] in_11,
  input  [7:0] in_12,
  input  [7:0] in_13,
  input  [7:0] in_14,
  input  [7:0] in_15,
  input  [7:0] in_16,
  input  [7:0] in_17,
  input  [7:0] in_18,
  input  [7:0] in_19,
  input  [7:0] in_20,
  input  [7:0] in_21,
  input  [7:0] in_22,
  input  [7:0] in_23,
  input  [7:0] in_24,
  input  [7:0] in_25,
  input  [7:0] in_26,
  input  [7:0] in_27,
  input  [7:0] in_28,
  input  [7:0] in_29,
  input  [7:0] in_30,
  input  [7:0] in_31,
  input  [7:0] in_32,
  output [63:0] out_33,
  output [63:0] out_34,
  output [63:0] out_35,
  output [63:0] out_36
);

  DotMatrix #(.matrixcols(16), .matrixrows(16)) dotmatrix_1 (
    .col0({in_1, in_17}), .col1({in_2, in_18}), .col2({in_3, in_19}), .col3({in_4, in_20}),
    .col4({in_5, in_21}), .col5({in_6, in_22}), .col6({in_7, in_23}), .col7({in_8, in_24}),
    .col8({in_9, in_25}), .col9({in_10, in_26}), .col10({in_11, in_27}), .col11({in_12, in_28}),
    .col12({in_13, in_29}), .col13({in_14, in_30}), .col14({in_15, in_31}), .col15({in_16, in_32}));

  assign out_33 = {in_13, in_29, in_14, in_30, in_15, in_31, in_16, in_32};
  assign out_34 = {in_1, in_17, in_2, in_18, in_3, in_19, in_4, in_20};
  assign out_35 = {in_9, in_25, in_10, in_26, in_11, in_27, in_12, in_28};
  assign out_36 = {in_5, in_21, in_6, in_22, in_7, in_23, in_8, in_24};
endmodule

module ChannelController (
  input  CLK,
  input  [1:0] in_2,
  output [63:0] L1,
  output [63:0] L2,
  output [63:0] L3,
  output [63:0] L4
);

  wire [63:0] channelanimation_1_out_2, channelanimation_1_out_3, channelanimation_1_out_4,
       channelanimation_1_out_5;

  ChannelAnimation channelanimation_1 (
    .CLK(CLK), .out_2(channelanimation_1_out_2), .out_3(channelanimation_1_out_3),
    .out_4(channelanimation_1_out_4), .out_5(channelanimation_1_out_5));
  Multiplexer #(.select(2), .width(64)) multiplexer_1 (
    .in0(channelanimation_1_out_2), .in1(64'h70009003303c2), .in2(64'h2080208061c04143),
    .in3(64'h102710251fe7002), .out(L1), .sel(in_2));
  Multiplexer #(.select(2), .width(64)) multiplexer_2 (
    .in0(channelanimation_1_out_3), .in1(64'hc34080810181024), .in2(64'h404e403040600f83),
    .in3(64'h23ffe20022002), .out(L2), .sel(in_2));
  Multiplexer #(.select(2), .width(64)) multiplexer_3 (
    .in0(channelanimation_1_out_4), .in1(64'h1044108831084a10), .in2(64'h103c20e049008880),
    .in3(64'h3ffe010401040ffc), .out(L3), .sel(in_2));
  Multiplexer #(.select(2), .width(64)) multiplexer_4 (
    .in0(channelanimation_1_out_5), .in1(64'h4c609b80a000c000), .in2(64'hc87838070fc0083e),
    .in3(64'h41ffc10041004), .out(L4), .sel(in_2));
  DotMatrix #(.matrixcols(16), .matrixrows(16)) dotmatrix_1 (
    .col0(L1[63:48]), .col1(L1[47:32]), .col2(L1[31:16]), .col3(L1[15:0]), .col4(L2[63:48]),
    .col5(L2[47:32]), .col6(L2[31:16]), .col7(L2[15:0]), .col8(L3[63:48]), .col9(L3[47:32]),
    .col10(L3[31:16]), .col11(L3[15:0]), .col12(L4[63:48]), .col13(L4[47:32]), .col14(L4[31:16]),
    .col15(L4[15:0]));
endmodule

module BusDriver (
  input  [63:0] D3,
  input  [63:0] D2,
  input  [63:0] D1,
  input  [63:0] D0,
  input  [63:0] C3,
  input  [63:0] C2,
  input  [63:0] C1,
  input  [63:0] C0,
  input  [63:0] B3,
  input  [63:0] B2,
  input  [63:0] B1,
  input  [63:0] B0,
  input  [63:0] A3,
  input  [63:0] A2,
  input  [63:0] A1,
  input  [63:0] A0,
  input  S0,
  input  S1,
  output [63:0] L1,
  output [63:0] L2,
  output [63:0] L3,
  output [63:0] L4
);

  wire oneoftwodecoder_1_y0, oneoftwodecoder_1_y1, oneoftwodecoder_1_y2, oneoftwodecoder_1_y3;

  OneOfTwoDecoder oneoftwodecoder_1 (
    .A(S0), .B(S1), .Y0(oneoftwodecoder_1_y0), .Y1(oneoftwodecoder_1_y1), .Y2(oneoftwodecoder_1_y2),
    .Y3(oneoftwodecoder_1_y3));
  assign L1 = oneoftwodecoder_1_y3 ? D3 : 64'bz;  // Controlled_Buffer controlled_buffer_1
  assign L1 = oneoftwodecoder_1_y0 ? A3 : 64'bz;  // Controlled_Buffer controlled_buffer_2
  assign L1 = oneoftwodecoder_1_y1 ? B3 : 64'bz;  // Controlled_Buffer controlled_buffer_3
  assign L1 = oneoftwodecoder_1_y2 ? C3 : 64'bz;  // Controlled_Buffer controlled_buffer_4
  assign L2 = oneoftwodecoder_1_y3 ? D2 : 64'bz;  // Controlled_Buffer controlled_buffer_5
  assign L2 = oneoftwodecoder_1_y0 ? A2 : 64'bz;  // Controlled_Buffer controlled_buffer_6
  assign L2 = oneoftwodecoder_1_y1 ? B2 : 64'bz;  // Controlled_Buffer controlled_buffer_7
  assign L2 = oneoftwodecoder_1_y2 ? C2 : 64'bz;  // Controlled_Buffer controlled_buffer_8
  assign L3 = oneoftwodecoder_1_y3 ? D1 : 64'bz;  // Controlled_Buffer controlled_buffer_9
  assign L3 = oneoftwodecoder_1_y0 ? A1 : 64'bz;  // Controlled_Buffer controlled_buffer_10
  assign L3 = oneoftwodecoder_1_y1 ? B1 : 64'bz;  // Controlled_Buffer controlled_buffer_11
  assign L3 = oneoftwodecoder_1_y2 ? C1 : 64'bz;  // Controlled_Buffer controlled_buffer_12
  assign L4 = oneoftwodecoder_1_y3 ? D0 : 64'bz;  // Controlled_Buffer controlled_buffer_13
  assign L4 = oneoftwodecoder_1_y0 ? A0 : 64'bz;  // Controlled_Buffer controlled_buffer_14
  assign L4 = oneoftwodecoder_1_y1 ? B0 : 64'bz;  // Controlled_Buffer controlled_buffer_15
  assign L4 = oneoftwodecoder_1_y2 ? C0 : 64'bz;  // Controlled_Buffer controlled_buffer_16
endmodule

module VolumeController (
  input  Up,
  input  Down,
  input  [1:0] ch,
  output [9:0] out_4,
  output [9:0] out_5,
  output [9:0] out_6,
  output [9:0] out_7
);

  wire demultiplexer_1_out0, demultiplexer_1_out1, demultiplexer_1_out2, demultiplexer_1_out3,
       demultiplexer_2_out0, demultiplexer_2_out1, demultiplexer_2_out2, demultiplexer_2_out3;

  Demultiplexer #(.select(2)) demultiplexer_1 (
    .out0(demultiplexer_1_out0), .out1(demultiplexer_1_out1), .out2(demultiplexer_1_out2),
    .out3(demultiplexer_1_out3), .in(Up), .sel(ch));
  Demultiplexer #(.select(2)) demultiplexer_2 (
    .out0(demultiplexer_2_out0), .out1(demultiplexer_2_out1), .out2(demultiplexer_2_out2),
    .out3(demultiplexer_2_out3), .in(Down), .sel(ch));
  DotMatrix #(.matrixcols(2), .matrixrows(10)) dotmatrix_1 (.col0(out_4), .col1(out_4));
  Volume volume_1 (.Up(demultiplexer_1_out0), .Down(demultiplexer_2_out0), .out_3(out_4));
  DotMatrix #(.matrixcols(2), .matrixrows(10)) dotmatrix_2 (.col0(out_5), .col1(out_5));
  Volume volume_2 (.Up(demultiplexer_1_out1), .Down(demultiplexer_2_out1), .out_3(out_5));
  DotMatrix #(.matrixcols(2), .matrixrows(10)) dotmatrix_3 (.col0(out_6), .col1(out_6));
  Volume volume_3 (.Up(demultiplexer_1_out2), .Down(demultiplexer_2_out2), .out_3(out_6));
  DotMatrix #(.matrixcols(2), .matrixrows(10)) dotmatrix_4 (.col0(out_7), .col1(out_7));
  Volume volume_4 (.Up(demultiplexer_1_out3), .Down(demultiplexer_2_out3), .out_3(out_7));
endmodule

module BCDCounter (
  input  in_1,
  output [9:0] out_2,
  output [7:0] out_3
);

  wire and_1_out;
  wire [3:0] j_k_ff_1_q;

  J_K_Flip_Flop #(.trigger("falling")) j_k_ff_1 (
    .J(1'b1), .K(1'b1), .clk(in_1), .Q(j_k_ff_1_q[0]), .reset(and_1_out));  // open: Qn, preset
  J_K_Flip_Flop #(.trigger("falling")) j_k_ff_2 (
    .J(1'b1), .K(1'b1), .clk(j_k_ff_1_q[0]), .Q(j_k_ff_1_q[1]), .reset(and_1_out));  // open: Qn, preset
  J_K_Flip_Flop #(.trigger("falling")) j_k_ff_3 (
    .J(1'b1), .K(1'b1), .clk(j_k_ff_1_q[1]), .Q(j_k_ff_1_q[2]), .reset(and_1_out));  // open: Qn, preset
  J_K_Flip_Flop #(.trigger("falling")) j_k_ff_4 (
    .J(1'b1), .K(1'b1), .clk(j_k_ff_1_q[2]), .Q(j_k_ff_1_q[3]), .reset(and_1_out));  // open: Qn, preset
  Hex_Digit_Display hex_digit_display_1 (.value(j_k_ff_1_q));  // open: dp
  and and_1 (and_1_out, j_k_ff_1_q[1], j_k_ff_1_q[3]);
  Shifter #(.shift("rl"), .width(10)) shifter_1 (.in(10'h1), .\dist (j_k_ff_1_q), .out(out_2));
  BitAdder #(.width(10)) bitadder_1 (.in0(out_2));  // open: in1, out

  assign out_3 = out_2[7:0];
endmodule

module StoSRegister (
  input  \bit ,
  input  Clock,
  output [9:0] Up,
  output [9:0] Down
);

  D_Flip_Flop d_ff_1 (.D(\bit ), .clk(Clock), .Q(Down[9]));  // open: Qn, preset, reset
  D_Flip_Flop d_ff_2 (.D(Down[9]), .clk(Clock), .Q(Down[8]));  // open: Qn, preset, reset
  D_Flip_Flop d_ff_3 (.D(Down[8]), .clk(Clock), .Q(Down[7]));  // open: Qn, preset, reset
  D_Flip_Flop d_ff_4 (.D(Down[7]), .clk(Clock), .Q(Down[6]));  // open: Qn, preset, reset
  D_Flip_Flop d_ff_5 (.D(Down[6]), .clk(Clock), .Q(Down[5]));  // open: Qn, preset, reset
  D_Flip_Flop d_ff_6 (.D(Down[5]), .clk(Clock), .Q(Down[4]));  // open: Qn, preset, reset
  D_Flip_Flop d_ff_7 (.D(Down[4]), .clk(Clock), .Q(Down[3]));  // open: Qn, preset, reset
  D_Flip_Flop d_ff_8 (.D(Down[3]), .clk(Clock), .Q(Down[2]));  // open: Qn, preset, reset
  D_Flip_Flop d_ff_9 (.D(Down[2]), .clk(Clock), .Q(Down[1]));  // open: Qn, preset, reset
  D_Flip_Flop d_ff_10 (.D(Down[1]), .clk(Clock), .Q(Down[0]));  // open: Qn, preset, reset

  assign Up = {Down[0], Down[1], Down[2], Down[3], Down[4], Down[5], Down[6], Down[7], Down[8], Down[9]};
endmodule

module BiShiftRegister (
  input  CLK,
  input  RL,
  output [9:0] out_3
);

  wire multiplexer_1_out, multiplexer_2_out, multiplexer_3_out, multiplexer_4_out, multiplexer_5_out,
       multiplexer_6_out, multiplexer_7_out, multiplexer_8_out, multiplexer_9_out, multiplexer_10_out;

  Multiplexer multiplexer_1 (.in0(out_3[8]), .in1(1'b0), .out(multiplexer_1_out), .sel(RL));
  D_Flip_Flop d_ff_1 (.D(multiplexer_1_out), .clk(CLK), .Q(out_3[9]));  // open: Qn, preset, reset
  Multiplexer multiplexer_2 (.in0(out_3[7]), .in1(out_3[9]), .out(multiplexer_2_out), .sel(RL));
  D_Flip_Flop d_ff_2 (.D(multiplexer_2_out), .clk(CLK), .Q(out_3[8]));  // open: Qn, preset, reset
  Multiplexer multiplexer_3 (.in0(out_3[6]), .in1(out_3[8]), .out(multiplexer_3_out), .sel(RL));
  D_Flip_Flop d_ff_3 (.D(multiplexer_3_out), .clk(CLK), .Q(out_3[7]));  // open: Qn, preset, reset
  Multiplexer multiplexer_4 (.in0(out_3[5]), .in1(out_3[7]), .out(multiplexer_4_out), .sel(RL));
  D_Flip_Flop d_ff_4 (.D(multiplexer_4_out), .clk(CLK), .Q(out_3[6]));  // open: Qn, preset, reset
  Multiplexer multiplexer_5 (.in0(out_3[4]), .in1(out_3[6]), .out(multiplexer_5_out), .sel(RL));
  D_Flip_Flop d_ff_5 (.D(multiplexer_5_out), .clk(CLK), .Q(out_3[5]));  // open: Qn, preset, reset
  Multiplexer multiplexer_6 (.in0(out_3[3]), .in1(out_3[5]), .out(multiplexer_6_out), .sel(RL));
  D_Flip_Flop d_ff_6 (.D(multiplexer_6_out), .clk(CLK), .Q(out_3[4]));  // open: Qn, preset, reset
  D_Flip_Flop d_ff_7 (.D(multiplexer_7_out), .clk(CLK), .Q(out_3[3]));  // open: Qn, preset, reset
  Multiplexer multiplexer_7 (.in0(out_3[2]), .in1(out_3[4]), .out(multiplexer_7_out), .sel(RL));
  D_Flip_Flop d_ff_8 (.D(multiplexer_8_out), .clk(CLK), .Q(out_3[2]));  // open: Qn, preset, reset
  Multiplexer multiplexer_8 (.in0(out_3[1]), .in1(out_3[3]), .out(multiplexer_8_out), .sel(RL));
  D_Flip_Flop d_ff_9 (.D(multiplexer_9_out), .clk(CLK), .Q(out_3[1]));  // open: Qn, preset, reset
  Multiplexer multiplexer_9 (.in0(out_3[0]), .in1(out_3[2]), .out(multiplexer_9_out), .sel(RL));
  D_Flip_Flop d_ff_10 (.D(multiplexer_10_out), .clk(CLK), .Q(out_3[0]));  // open: Qn, preset, reset
  Multiplexer multiplexer_10 (.in0(1'b1), .in1(out_3[1]), .out(multiplexer_10_out), .sel(RL));
endmodule

module Volume (
  input  Up,
  input  Down,
  output [9:0] out_3
);

  wire d_ff_1_q, multiplexer_1_out, not_1_out;

  not not_1 (not_1_out, d_ff_1_q);
  Multiplexer multiplexer_1 (.in0(Down), .in1(Up), .out(multiplexer_1_out), .sel(Up));
  D_Flip_Flop d_ff_1 (.D(Up), .clk(multiplexer_1_out), .Q(d_ff_1_q));  // open: Qn, preset, reset
  BiShiftRegister bishiftregister_1 (.CLK(multiplexer_1_out), .RL(not_1_out), .out_3(out_3));
  DotMatrix #(.matrixcols(2), .matrixrows(10)) dotmatrix_1 (.col0(out_3), .col1(out_3));
endmodule

module ChannelAnimation (
  input  CLK,
  output [63:0] out_2,
  output [63:0] out_3,
  output [63:0] out_4,
  output [63:0] out_5
);

  wire [1:0] twobitcounter_1_d;

  TwoBitCounter twobitcounter_1 (.CLK(CLK), .D(twobitcounter_1_d));
  BusDriver busdriver_1 (
    .D3(64'h1cf01cf0000000), .D2(64'h78007800000003c), .D1(64'h3c7c007c000000), .D0(64'h1c001c3f003f),
    .C3(64'h38f838f8000000), .C2(64'hf000f000000001e), .C1(64'h1ef800f8000000), .C0(64'he000e7e007e),
    .B3(64'h707c707c000000), .B2(64'h1e001e000000000f), .B1(64'hff000f0000000), .B0(64'h70007fc00fc),
    .A3(64'he03ee03e000000), .A2(64'h3c003c0000000007), .A1(64'h7e000e0000000), .A0(64'h38003f801f8),
    .S0(twobitcounter_1_d[0]), .S1(twobitcounter_1_d[1]), .L1(out_2), .L2(out_3), .L3(out_4), .L4(out_5));
endmodule
